# Fritzing sketch MicroPython_SPBTLERF_Breakout_v01_mod (saved by Fritzing 0.9.3b)
circuit board: 3.30722cm x 4.20939cm
breadboards: 1

parts:
  U2 = SPBTLE-RF [package=xcvr_spbtle-rf]
  R2 = Resistor [tolerance=±5% resistance=47k package="0603 [SMD]"]
  R3 = Resistor [tolerance=±5% resistance=10k package="0603 [SMD]"]
  R1 = Resistor [tolerance=±5% resistance=10k package="0603 [SMD]"]
  C1 = Ceramic Capacitor [capacitance=470µF voltage=16V package="0603 [SMD, multilayer]"]
  Q1 = PNP-Transistor [package="SOT-23 [SMD]"]
  R5 = Resistor [tolerance=±5% resistance=47 package="0603 [SMD]"]
  pyboard1 = Micro Python pyboard [part_number=PYBv10b]
  R4 = Resistor [tolerance=±5% resistance=47 package="0603 [SMD]"]

nets:
  N1: U2.SPI_IRQ, R2.Pin_1
  N2: U2.VIN, C1.1, Q1.1
  N3: U2.GND, C1.0, pyboard1.Y14_GND
  N4: U2.SPI_CLK, pyboard1.Y6
  N5: U2.SPI_MISO, pyboard1.Y7
  N6: U2.SPI_MOSI, pyboard1.Y8
  N7: U2.SPI_CS, R1.Pin_0
  N8: U2.BT_RESET, R3.Pin_1
  N9: R2.Pin_0, pyboard1.Y3
  N10: R3.Pin_0, pyboard1.Y4
  N11: R1.Pin_1, pyboard1.Y5
  N12: Q1.2, pyboard1.Y15_3V3, R4.Pin_1
  N13: Q1.0, R5.Pin_1, R4.Pin_0
  N14: R5.Pin_0, pyboard1.X8

notes:
  C1 : supply power input(VCC) -> X7
  C2 : reset signal input(RST) -> X4
  C3 : clock signal input(CLK) -> X5
  C5 : ground(GND, reference voltage) -> ??
  C6 : standard or proprietary use(SPU) -> ??
  C7: input/output for serial data(I/O) -> X3
  uBLE v0.1

custom parts:
  SPBTLE-RF: Very low power module for Bluetooth Smart v4.1
