# Fritzing sketch MicroPython_SPBTLERF_Breakout_v03_mod (saved by Fritzing 0.9.3b)
circuit board: 3.30722cm x 4.20939cm
breadboards: 1

parts:
  U2 = SPBTLE-RF [package=xcvr_spbtle-rf]
  C1 = Ceramic Capacitor [capacitance=470µF voltage=16V package="0603 [SMD, multilayer]"]
  pyboard1 = Micro Python pyboard [part_number=PYBv10b]

nets:
  N1: U2.SPI_IRQ, pyboard1.Y3
  N2: U2.VIN, C1.1, pyboard1.Y15_3V3
  N3: U2.GND, C1.0, pyboard1.Y14_GND
  N4: U2.SPI_CLK, pyboard1.Y6
  N5: U2.SPI_MISO, pyboard1.Y7
  N6: U2.SPI_MOSI, pyboard1.Y8
  N7: U2.SPI_CS, pyboard1.Y5
  N8: U2.BT_RESET, pyboard1.Y4

notes:
  C1 : supply power input(VCC) -> X7
  C2 : reset signal input(RST) -> X4
  C3 : clock signal input(CLK) -> X5
  C5 : ground(GND, reference voltage) -> ??
  C6 : standard or proprietary use(SPU) -> ??
  C7: input/output for serial data(I/O) -> X3
  uBLE v0.3

custom parts:
  SPBTLE-RF: Very low power module for Bluetooth Smart v4.1
